# Fritzing sketch Bolu Reciever (2) (saved by Fritzing 0.9.3b)
breadboards: 1

parts:
  part = cc1101 module
  Part1 = Arduino Nano (Rev3.0) (ICSP)
  9V = LIPO-1000mAh [package=lipo-1000]
  12V_Bulb = Super Flux LED blue [color=Blue]
  relay = KY-019 5V Relay Module [package="Breakout board"]

nets:
  N1: part.pin_2, Part1.3V3
  N2: part.pin_3, Part1.D11/MOSI
  N3: part.pin_4, Part1.D13/SCK
  N4: part.pin_5, Part1.D12/MISO
  N5: part.pin_7, Part1.D10
  N6: part.pin_8, Part1.D2
  N7: part.pin_9, Part1.GND, 9V.+, 12V_Bulb.anode
  N8: Part1.D6, relay.S
  N9: Part1.VIN, 9V.-, relay.+, relay.Common
  N10: 12V_Bulb.cathode, relay.NO

custom parts:
  cc1101 module: CC1101 rf module.
  KY-019 5V Relay Module: KY-019 5V Relay module, used to control AC circuits. (Special thanks to vanepp for fixing the PCB holes and other errors)
