# Fritzing sketch Bolu Reciever (saved by Fritzing 0.9.3b)
breadboards: 1

parts:
  part = cc1101 module
  Part1 = Arduino Nano (Rev3.0) (ICSP)
  9V = LIPO-1000mAh [package=lipo-1000]
  PIR_Motion_Sensor = PIR sensor
  PIR_Motion_Sensor1 = PIR sensor
  PIR_Motion_Sensor2 = PIR sensor

nets:
  N1: part.pin_2, Part1.3V3
  N2: part.pin_3, Part1.D11/MOSI
  N3: part.pin_4, Part1.D13/SCK
  N4: part.pin_5, Part1.D12/MISO
  N5: part.pin_7, Part1.D10
  N6: part.pin_8, Part1.D2
  GND: part.pin_9, part.pin_10, Part1.GND, 9V.+, PIR_Motion_Sensor.GND, PIR_Motion_Sensor1.GND, PIR_Motion_Sensor2.GND
  N7: Part1.D5, PIR_Motion_Sensor2.SIG
  N8: Part1.D6, PIR_Motion_Sensor.SIG
  N9: Part1.D7, PIR_Motion_Sensor1.SIG
  VDD: Part1.VIN, 9V.-, PIR_Motion_Sensor.VDD, PIR_Motion_Sensor1.VDD, PIR_Motion_Sensor2.VDD

custom parts:
  cc1101 module: CC1101 rf module.
